# Fritzing sketch Circuit (saved by Fritzing 0.9.3b)
breadboards: 1

parts:
  VCC1 = Battery block 9V
  U1 = NodeMCU V1.0
  LED1 = smd LED [color="Red (633nm)" package="1206 [SMD]"]
  MAX471_Current_and_Voltage_Sensor1 = MAX471 Current and Voltage Sensor Module
  LED2 = smd LED [color="Blue (525nm)" package="0805 [SMD]"]
  TTP223B1 = TTP223B Capacitive Touch Sensor Module
  R1 = Resistor [tolerance=±5% resistance=145 package=THT]
  R2 = Resistor [tolerance=±5% resistance=396 package=THT]
  CD1 = CD4051
  Q3 = 2N7000 FET N-Channel [part_number=2N7000 package=TO92]

nets:
  GND: VCC1.-, U1.GND, MAX471_Current_and_Voltage_Sensor1.GND#12, LED2.cathode, TTP223B1.GND, CD1.Inhibit, CD1.VEE, CD1.VSS, CD1.Input_C, CD1.Input_B
  VIN: VCC1.+, U1.Vin, MAX471_Current_and_Voltage_Sensor1.VOUT, MAX471_Current_and_Voltage_Sensor1.VIN, R2.Pin_1, Q3.source
  N1: U1.D0, Q3.gate
  N2: U1.D1, CD1.Input_A
  N3: U1.D2, R1.Pin_1
  3V3: U1.3V3, TTP223B1.VCC, CD1.VDD
  N4: U1.D8, TTP223B1.SIG
  N5: U1.A0, CD1.In/Out
  N6: LED1.cathode, MAX471_Current_and_Voltage_Sensor1.GND#8, Q3.drain
  N7: LED1.anode, R2.Pin_0
  N8: MAX471_Current_and_Voltage_Sensor1.AT, CD1.Chan_1
  N9: MAX471_Current_and_Voltage_Sensor1.VT, CD1.Chan_0
  N10: LED2.anode, R1.Pin_0

custom parts:
  NodeMCU V1.0: ESP8266 based NodeMCU
  MAX471 Current and Voltage Sensor Module: The MAX471 current and voltage sensor module is a bidirectional, highside current-sense amplifier. The current measurement maximum is 3 amps and the voltage measurement range is 3 to 25 volts. The operating voltage range is 3 to 36 volts.
  TTP223B Capacitive Touch Sensor Module: The TTP223B capacitive touch sensor module uses the TTP223B IC. The appropriate voltage is approximately 2 to 5.5 volts.
  2N7000 FET N-Channel: A 2N7000 MOSFET N-Channel Transistor
